// Logisim project AtividadePratica1.circ as structural Verilog: 5 circuits, main circuit main
module main (
  input  x0,
  input  x1,
  input  x2,
  input  x3,
  input  in_5,
  input  y0,
  input  y1,
  input  y2,
  input  y3
);

  wire DecodeSum_a, DecodeSum_b, DecodeSum_c, DecodeSum_d, DecodeSum_e, DecodeSum_f, DecodeSum_g, DecodeX_a,
       DecodeX_b, DecodeX_c, DecodeX_d, DecodeX_e, DecodeX_f, DecodeX_g, DecodeY_a, DecodeY_b, DecodeY_c,
       DecodeY_d, DecodeY_e, DecodeY_f, DecodeY_g, Sum4bits_s0, Sum4bits_s1, Sum4bits_s2, Sum4bits_s3;

  Soma4bits Sum4bits (
    .x0(x0), .y0(y0), .x1(x1), .y1(y1), .x2(x2), .y2(y2), .x3(x3), .y3(y3), .in_1(in_5), .s0(Sum4bits_s0),
    .s1(Sum4bits_s1), .s2(Sum4bits_s2), .s3(Sum4bits_s3));  // open: out_14
  Decode4p7 DecodeX (
    .E3(x3), .E2(x2), .E1(x1), .E0(x0), .a(DecodeX_a), .b(DecodeX_b), .c(DecodeX_c), .d(DecodeX_d),
    .e(DecodeX_e), .f(DecodeX_f), .g(DecodeX_g));
  Decode4p7 DecodeY (
    .E3(y3), .E2(y2), .E1(y1), .E0(y0), .a(DecodeY_a), .b(DecodeY_b), .c(DecodeY_c), .d(DecodeY_d),
    .e(DecodeY_e), .f(DecodeY_f), .g(DecodeY_g));
  _7_Segment_Display u_7_segment_display_1 (
    .g(DecodeX_g), .f(DecodeX_f), .a(DecodeX_a), .b(DecodeX_b), .e(DecodeX_e), .d(DecodeX_d), .c(DecodeX_c));  // open: dp
  _7_Segment_Display u_7_segment_display_2 (
    .g(DecodeY_g), .f(DecodeY_f), .a(DecodeY_a), .b(DecodeY_b), .e(DecodeY_e), .d(DecodeY_d), .c(DecodeY_c));  // open: dp
  Decode4p7 DecodeSum (
    .E3(Sum4bits_s3), .E2(Sum4bits_s2), .E1(Sum4bits_s1), .E0(Sum4bits_s0), .a(DecodeSum_a), .b(DecodeSum_b),
    .c(DecodeSum_c), .d(DecodeSum_d), .e(DecodeSum_e), .f(DecodeSum_f), .g(DecodeSum_g));
  _7_Segment_Display u_7_segment_display_3 (
    .g(DecodeSum_g), .f(DecodeSum_f), .a(DecodeSum_a), .b(DecodeSum_b), .e(DecodeSum_e), .d(DecodeSum_d),
    .c(DecodeSum_c));  // open: dp
endmodule

module meiaSoma (
  input  x,
  input  y,
  output s,
  output vai1
);

  and and_1 (vai1, y, x);
  xor xor_1 (s, x, y);
endmodule

module SomaCompleta (
  input  vem1,
  input  Xn,
  input  Yn,
  output Sn,
  output VAI1n
);

  wire meiasoma_1_s, meiasoma_1_vai1, meiasoma_2_vai1;

  meiaSoma meiasoma_1 (.x(Xn), .y(Yn), .vai1(meiasoma_1_vai1), .s(meiasoma_1_s));
  or or_1 (VAI1n, meiasoma_1_vai1, meiasoma_2_vai1);
  meiaSoma meiasoma_2 (.x(vem1), .y(meiasoma_1_s), .vai1(meiasoma_2_vai1), .s(Sn));
endmodule

module Soma4bits (
  input  in_1,
  input  x0,
  input  y0,
  input  x1,
  input  y1,
  input  x2,
  input  y2,
  input  x3,
  input  y3,
  output s0,
  output s1,
  output s2,
  output s3,
  output out_14
);

  wire somacompleta_1_vai1n, somacompleta_2_vai1n, somacompleta_3_vai1n;

  SomaCompleta somacompleta_1 (.Xn(x0), .Yn(y0), .vem1(in_1), .VAI1n(somacompleta_1_vai1n), .Sn(s0));
  SomaCompleta somacompleta_2 (.Xn(x1), .Yn(y1), .vem1(somacompleta_1_vai1n), .VAI1n(somacompleta_2_vai1n), .Sn(s1));
  SomaCompleta somacompleta_3 (.Xn(x2), .Yn(y2), .vem1(somacompleta_2_vai1n), .VAI1n(somacompleta_3_vai1n), .Sn(s2));
  SomaCompleta somacompleta_4 (.Xn(x3), .Yn(y3), .vem1(somacompleta_3_vai1n), .VAI1n(out_14), .Sn(s3));
endmodule

module Decode4p7 (
  input  E3,
  input  E2,
  input  E1,
  input  E0,
  output a,
  output b,
  output c,
  output d,
  output e,
  output f,
  output g
);

  wire and_1_out, and_2_out, and_3_out, and_4_out, and_5_out, and_6_out, and_7_out, and_8_out, and_9_out,
       and_10_out, and_11_out, and_12_out, and_13_out, and_14_out, and_15_out, and_16_out, and_17_out,
       and_18_out, and_19_out, and_20_out, and_21_out, and_22_out, and_23_out, and_24_out, and_25_out,
       and_26_out, and_27_out, and_28_out, and_29_out, and_30_out, and_31_out, and_32_out, and_33_out,
       and_34_out, and_35_out, and_36_out, and_37_out, and_38_out, and_39_out, and_40_out, and_41_out,
       and_42_out, and_43_out, and_44_out, and_45_out, and_46_out, and_47_out, not_1_out, not_2_out,
       not_3_out, not_4_out, not_5_out, not_6_out, not_7_out, not_8_out, not_9_out, not_10_out, not_11_out,
       not_12_out, not_13_out, not_14_out, not_15_out, not_16_out, not_17_out, not_18_out, not_19_out,
       not_20_out, not_21_out, not_22_out, not_23_out, not_24_out, not_25_out, not_26_out, not_27_out,
       not_28_out, not_29_out, not_30_out, not_31_out, not_32_out, not_33_out, not_34_out, not_35_out,
       not_36_out, not_37_out, not_38_out, not_39_out, not_40_out, not_41_out, not_42_out, not_43_out,
       not_44_out, or_1_out, or_2_out, or_3_out, or_4_out, or_5_out, or_6_out, or_7_out, or_8_out, or_9_out,
       or_10_out, or_12_out, or_13_out, or_14_out, or_15_out, or_16_out, or_17_out, or_18_out, or_20_out,
       or_21_out, or_22_out, or_23_out;

  not not_1 (not_1_out, E2);
  not not_2 (not_2_out, E0);
  not not_3 (not_3_out, E3);
  not not_4 (not_4_out, E3);
  and and_1 (and_1_out, E3, not_5_out);
  not not_5 (not_5_out, E2);
  not not_6 (not_6_out, E1);
  not not_7 (not_7_out, E3);
  not not_8 (not_8_out, E2);
  not not_9 (not_9_out, E3);
  and and_2 (and_2_out, not_9_out, not_10_out);
  not not_10 (not_10_out, E1);
  not not_11 (not_11_out, E0);
  not not_12 (not_12_out, E3);
  not not_13 (not_13_out, E1);
  not not_14 (not_14_out, E3);
  and and_3 (and_3_out, not_14_out, not_15_out);
  not not_15 (not_15_out, E1);
  not not_16 (not_16_out, E3);
  and and_4 (and_4_out, not_16_out, E0);
  not not_17 (not_17_out, E1);
  not not_18 (not_18_out, E3);
  not not_19 (not_19_out, E2);
  not not_20 (not_20_out, E3);
  and and_5 (and_5_out, not_20_out, not_21_out);
  not not_21 (not_21_out, E2);
  not not_22 (not_22_out, E0);
  not not_23 (not_23_out, E2);
  and and_6 (and_6_out, not_23_out, E1);
  not not_24 (not_24_out, E1);
  not not_25 (not_25_out, E1);
  not not_26 (not_26_out, E2);
  and and_7 (and_7_out, not_26_out, not_27_out);
  not not_27 (not_27_out, E0);
  and and_8 (and_8_out, E1, not_28_out);
  not not_28 (not_28_out, E0);
  and and_9 (and_9_out, E3, E1);
  and and_10 (and_10_out, E3, E2);
  not not_29 (not_29_out, E1);
  not not_30 (not_30_out, E0);
  not not_31 (not_31_out, E3);
  and and_11 (and_11_out, not_31_out, E2);
  not not_32 (not_32_out, E1);
  not not_33 (not_33_out, E2);
  and and_12 (and_12_out, not_33_out, E1);
  and and_13 (and_13_out, E1, not_34_out);
  not not_34 (not_34_out, E0);
  not not_35 (not_35_out, E3);
  and and_14 (and_14_out, not_35_out, E2);
  not not_36 (not_36_out, E1);
  not not_37 (not_37_out, E2);
  and and_15 (and_15_out, not_1_out, not_2_out);
  and and_16 (and_16_out, not_3_out, E1);
  and and_17 (and_17_out, not_4_out, E2);
  and and_18 (and_18_out, E2, E1);
  and and_19 (and_19_out, and_1_out, not_6_out);
  not not_38 (not_38_out, E0);
  and and_20 (and_20_out, not_7_out, not_8_out);
  and and_21 (and_21_out, and_2_out, not_11_out);
  not not_39 (not_39_out, E2);
  not not_40 (not_40_out, E0);
  and and_22 (and_22_out, not_12_out, E1);
  and and_23 (and_23_out, E3, not_13_out);
  or or_1 (or_1_out, and_3_out, and_4_out);
  and and_24 (and_24_out, not_17_out, E0);
  and and_25 (and_25_out, not_18_out, E2);
  and and_26 (and_26_out, E3, not_19_out);
  and and_27 (and_27_out, and_5_out, not_22_out);
  and and_28 (and_28_out, and_6_out, E0);
  and and_29 (and_29_out, E2, not_24_out);
  and and_30 (and_30_out, E2, E1);
  not not_41 (not_41_out, E0);
  and and_31 (and_31_out, E3, not_25_out);
  not not_42 (not_42_out, E0);
  or or_2 (or_2_out, and_7_out, and_8_out);
  or or_3 (or_3_out, and_9_out, and_10_out);
  and and_32 (and_32_out, not_29_out, not_30_out);
  and and_33 (and_33_out, and_11_out, not_32_out);
  not not_43 (not_43_out, E0);
  not not_44 (not_44_out, E2);
  or or_4 (or_4_out, and_12_out, and_13_out);
  and and_34 (and_34_out, and_14_out, not_36_out);
  and and_35 (and_35_out, E3, not_37_out);
  and and_36 (and_36_out, E3, E0);
  or or_5 (or_5_out, and_15_out, and_16_out);
  and and_37 (and_37_out, and_17_out, E0);
  or or_6 (or_6_out, and_18_out, and_19_out);
  and and_38 (and_38_out, E3, not_38_out);
  or or_7 (or_7_out, and_20_out, and_21_out);
  and and_39 (and_39_out, not_39_out, not_40_out);
  and and_40 (and_40_out, and_22_out, E0);
  and and_41 (and_41_out, and_23_out, E0);
  or or_8 (or_8_out, or_1_out, and_24_out);
  or or_9 (or_9_out, and_25_out, and_26_out);
  or or_10 (or_10_out, and_27_out, and_28_out);
  and and_42 (and_42_out, and_29_out, E0);
  and and_43 (and_43_out, and_30_out, not_41_out);
  and and_44 (and_44_out, and_31_out, not_42_out);
  or or_11 (e, or_2_out, or_3_out);
  or or_12 (or_12_out, and_32_out, and_33_out);
  and and_45 (and_45_out, E2, not_43_out);
  and and_46 (and_46_out, E3, not_44_out);
  and and_47 (and_47_out, E3, E1);
  or or_13 (or_13_out, or_4_out, and_34_out);
  or or_14 (or_14_out, and_35_out, and_36_out);
  or or_15 (or_15_out, or_5_out, and_37_out);
  or or_16 (or_16_out, or_6_out, and_38_out);
  or or_17 (or_17_out, or_7_out, and_39_out);
  or or_18 (or_18_out, and_40_out, and_41_out);
  or or_19 (c, or_8_out, or_9_out);
  or or_20 (or_20_out, or_10_out, and_42_out);
  or or_21 (or_21_out, and_43_out, and_44_out);
  or or_22 (or_22_out, or_12_out, and_45_out);
  or or_23 (or_23_out, and_46_out, and_47_out);
  or or_24 (g, or_13_out, or_14_out);
  or or_25 (a, or_15_out, or_16_out);
  or or_26 (b, or_17_out, or_18_out);
  or or_27 (d, or_20_out, or_21_out);
  or or_28 (f, or_22_out, or_23_out);
endmodule
