// Logisim project ULA_1bit.circ as structural Verilog: 3 circuits, main circuit ULA_1bit
module multiplex_1selector (
  input  a,
  input  b,
  input  select,
  output out_4
);

  wire and_1_out, and_2_out, not_1_out;

  not not_1 (not_1_out, select);
  and and_1 (and_1_out, a, not_1_out);
  and and_2 (and_2_out, b, select);
  or or_1 (out_4, and_1_out, and_2_out);
endmodule

module multiplex_2selector (
  input  a,
  input  b,
  input  c,
  input  d,
  input  Slct1,
  input  Slct2,
  output S
);

  wire and_1_out, and_2_out, and_3_out, and_4_out, not_1_out, not_2_out, not_3_out, not_4_out;

  not not_1 (not_1_out, Slct1);
  not not_2 (not_2_out, Slct2);
  not not_3 (not_3_out, Slct1);
  not not_4 (not_4_out, Slct2);
  and and_1 (and_1_out, a, not_1_out, not_2_out);
  and and_2 (and_2_out, b, not_3_out, Slct2);
  and and_3 (and_3_out, c, Slct1, not_4_out);
  and and_4 (and_4_out, d, Slct1, Slct2);
  or or_1 (S, and_1_out, and_2_out, and_3_out, and_4_out);
endmodule

module ULA_1bit (
  input  bitInvert,
  input  Carry_In,
  input  E0,
  input  E1,
  input  slct0,
  input  slct1,
  output S,
  output Carry_Out
);

  wire adder_1_out, and_1_out, multiplexer_1_out, not_1_out, not_2_out, or_1_out;

  Multiplexer #(.enable("false")) multiplexer_1 (.in0(E1), .in1(not_1_out), .out(multiplexer_1_out), .sel(bitInvert));
  not not_1 (not_1_out, E1);
  and and_1 (and_1_out, E0, multiplexer_1_out);
  or or_1 (or_1_out, E0, multiplexer_1_out);
  not not_2 (not_2_out, E0);
  Adder #(.width(1)) adder_1 (.a(E0), .b(multiplexer_1_out), .out(adder_1_out), .cin(Carry_In), .cout(Carry_Out));
  multiplex_2selector multiplex_2selector_1 (
    .a(and_1_out), .b(or_1_out), .c(not_2_out), .d(adder_1_out), .Slct1(slct0), .Slct2(slct1), .S(S));
endmodule
