// Logisim project ULA_4bit.circ as structural Verilog: 3 circuits, main circuit ULA_4bit
module ULA_1bit (
  input  bitInvert,
  input  Carry_In,
  input  E0,
  input  E1,
  input  slct0,
  input  slct1,
  output S,
  output Carry_Out
);

  wire adder_1_out, and_1_out, multiplexer_1_out, not_1_out, not_2_out, or_1_out;

  Multiplexer #(.enable("false")) multiplexer_1 (.in0(E1), .in1(not_1_out), .out(multiplexer_1_out), .sel(bitInvert));
  not not_1 (not_1_out, E1);
  and and_1 (and_1_out, E0, multiplexer_1_out);
  or or_1 (or_1_out, E0, multiplexer_1_out);
  not not_2 (not_2_out, E0);
  Adder #(.width(1)) adder_1 (.a(E0), .b(multiplexer_1_out), .out(adder_1_out), .cin(Carry_In), .cout(Carry_Out));
  Mux_2selectors mux_2selectors_1 (
    .a(and_1_out), .b(or_1_out), .c(not_2_out), .d(adder_1_out), .Slct1(slct0), .Slct2(slct1), .S(S));
endmodule

module ULA_4bit (
  input  bitInvert,
  input  X0,
  input  Y0,
  input  X1,
  input  Y1,
  input  X2,
  input  Y2,
  input  X3,
  input  Y3,
  input  slct0,
  input  slct1,
  output s0,
  output s1,
  output s2,
  output s3,
  output out_16
);

  wire ula_1bit_1_carry_out, ula_1bit_2_carry_out, ula_1bit_3_carry_out;

  ULA_1bit ula_1bit_1 (
    .E0(X0), .E1(Y0), .bitInvert(bitInvert), .Carry_In(bitInvert), .Carry_Out(ula_1bit_1_carry_out),
    .slct0(slct0), .slct1(slct1), .S(s0));
  ULA_1bit ula_1bit_2 (
    .E0(X1), .E1(Y1), .bitInvert(bitInvert), .Carry_In(ula_1bit_1_carry_out),
    .Carry_Out(ula_1bit_2_carry_out), .slct0(slct0), .slct1(slct1), .S(s1));
  ULA_1bit ula_1bit_3 (
    .E0(X2), .E1(Y2), .bitInvert(bitInvert), .Carry_In(ula_1bit_2_carry_out),
    .Carry_Out(ula_1bit_3_carry_out), .slct0(slct0), .slct1(slct1), .S(s2));
  ULA_1bit ula_1bit_4 (
    .E0(X3), .E1(Y3), .bitInvert(bitInvert), .Carry_In(ula_1bit_3_carry_out), .Carry_Out(out_16),
    .slct0(slct0), .slct1(slct1), .S(s3));
endmodule

module Mux_2selectors (
  input  a,
  input  b,
  input  c,
  input  d,
  input  Slct1,
  input  Slct2,
  output S
);

  wire and_1_out, and_2_out, and_3_out, and_4_out, not_1_out, not_2_out, not_3_out, not_4_out;

  not not_1 (not_1_out, Slct1);
  not not_2 (not_2_out, Slct2);
  not not_3 (not_3_out, Slct1);
  not not_4 (not_4_out, Slct2);
  and and_1 (and_1_out, a, not_1_out, not_2_out);
  and and_2 (and_2_out, b, not_3_out, Slct2);
  and and_3 (and_3_out, c, Slct1, not_4_out);
  and and_4 (and_4_out, d, Slct1, Slct2);
  or or_1 (S, and_1_out, and_2_out, and_3_out, and_4_out);
endmodule
