// Logisim project ULA_74181.circ as structural Verilog: 1 circuit, main circuit ULA_74181
module ULA_74181 (
  input  [3:0] A,
  input  [3:0] Selector,
  input  [3:0] B,
  output [3:0] S
);

  wire [3:0] and_1_out, and_2_out, and_3_out, and_4_out, nand_1_out, nor_1_out, not_1_out, not_2_out,
       or_1_out, or_2_out, or_3_out, or_4_out, xnor_1_out, xor_1_out;

  assign not_1_out = ~A;  // NOT_Gate not_1, 4 bits wide
  assign not_2_out = ~B;  // NOT_Gate not_2, 4 bits wide
  assign nor_1_out = ~(A | B);  // NOR_Gate nor_1, 4 bits wide
  assign and_1_out = not_1_out & B;  // AND_Gate and_1, 4 bits wide
  assign and_2_out = A & not_1_out;  // AND_Gate and_2, 4 bits wide
  assign nand_1_out = ~(A & B);  // NAND_Gate nand_1, 4 bits wide
  assign xor_1_out = A ^ B;  // XOR_Gate xor_1, 4 bits wide
  assign and_3_out = A & not_2_out;  // AND_Gate and_3, 4 bits wide
  assign or_1_out = not_1_out | B;  // OR_Gate or_1, 4 bits wide
  assign xnor_1_out = ~(A ^ B);  // XNOR_Gate xnor_1, 4 bits wide
  assign and_4_out = A & B;  // AND_Gate and_4, 4 bits wide
  assign or_2_out = not_2_out | B;  // OR_Gate or_2, 4 bits wide
  assign or_3_out = A | not_2_out;  // OR_Gate or_3, 4 bits wide
  assign or_4_out = A | B;  // OR_Gate or_4, 4 bits wide
  Multiplexer #(.select(4), .width(4), .enable("false")) multiplexer_1 (
    .in0(not_1_out), .in1(nor_1_out), .in2(and_1_out), .in3(and_2_out), .in4(nand_1_out), .in5(not_2_out),
    .in6(xor_1_out), .in7(and_3_out), .in8(or_1_out), .in9(xnor_1_out), .in10(B), .in11(and_4_out),
    .in12(or_2_out), .in13(or_3_out), .in14(or_4_out), .in15(A), .out(S), .sel(Selector));
endmodule
